// Logisim project design.circ as structural Verilog: 2 circuits, main circuit main
module main (
);

  wire ADC_out, ADD_out, adder_3_cout, and_1_out, and_2_out, and_3_out, and_4_out, and_5_out, and_6_out,
       and_7_out, and_8_out, and_9_out, and_10_out, and_11_out, and_13_out, Bit_2_out, Bit_3_out, Bit_4_out,
       Bit_5_out, Bit_out, C_2_out, C_out, Carry_flag_q, CF_out, Clock_out, decoder_1_out0, decoder_1_out1,
       decoder_1_out2, decoder_1_out3, decoder_2_out1, decoder_2_out2, decoder_2_out3, decoder_2_out4,
       decoder_2_out5, decoder_2_out6, decoder_2_out7, decoder_2_out8, decoder_2_out9, decoder_2_out10,
       decoder_2_out11, decoder_2_out12, decoder_2_out13, decoder_2_out14, decoder_2_out15, decoder_2_out16,
       decoder_2_out17, decoder_2_out18, decoder_2_out19, decoder_2_out20, decoder_2_out31, decoder_3_out0,
       decoder_3_out1, ENABLE_out, JA_2_out, JA_out, JC_out, JMP_2_out, JMP_3_out, JMP_4_out, JMP_5_out,
       JMP_6_out, JMP_out, JNA_2_out, JNA_out, JNC_out, JNZ_out, JZ_out, NO_CMP_out, nor_1_out, nor_2_out,
       nor_3_out, nor_4_out, not_1_out, not_2_out, not_3_out, not_4_out, not_6_out, or_1_out, or_2_out,
       Reset_out, S_C_out, SBB_out, Stop_running_qn, SUB_out, Zero_flag_q, ZF_out;
  wire [1:0] adder_2_out, Step_q;
  wire [2:0] multiplexer_4_out, n3_bit_dedecoder_1_out_8;
  wire [7:0] A_q, adder_1_out, adder_3_out, and_12_out, B_q, Data_byte_q, Instruction_byte_q,
       Instruction_pointer_q, multiplexer_1_out, multiplexer_2_out, multiplexer_3_out, multiplexer_5_out,
       multiplexer_6_out, multiplexer_7_out, multiplexer_8_out, not_5_out, not_7_out, or_3_out, ram_1_data,
       shifter_1_out, shifter_2_out, xor_1_out;
  wire [7:3] multiplexer_4_out_2;

  Clock Clock (.out(Clock_out));
  Button Reset (.out(Reset_out));
  D_Flip_Flop Stop_running (
    .clk(decoder_2_out31), .D(decoder_2_out31), .Qn(Stop_running_qn), .reset(Reset_out));  // open: Q, preset, en
  and and_1 (and_1_out, Stop_running_qn, Clock_out);
  Adder adder_1 (.a(Instruction_pointer_q), .b(8'h1), .out(adder_1_out));  // open: cin, cout
  Register Instruction_pointer (
    .D(multiplexer_1_out), .en(or_1_out), .Q(Instruction_pointer_q), .clk(and_1_out), .clr(Reset_out));
  Multiplexer #(.width(8), .enable("false")) multiplexer_1 (
    .in0(adder_1_out), .in1({multiplexer_4_out_2, multiplexer_4_out}), .out(multiplexer_1_out),
    .sel(JMP_6_out));
  or or_1 (or_1_out, JMP_6_out, not_1_out);
  not not_1 (not_1_out, decoder_1_out2);
  Adder #(.width(2)) adder_2 (.a(Step_q), .b(2'b01), .out(adder_2_out));  // open: cin, cout
  Register #(.width(2)) Step (.D(adder_2_out), .Q(Step_q), .clk(and_1_out), .clr(or_2_out));  // open: en
  or or_2 (or_2_out, Reset_out, decoder_1_out3);
  Multiplexer #(.width(8), .enable("false")) multiplexer_2 (
    .in0(Instruction_pointer_q), .in1(multiplexer_3_out), .out(multiplexer_2_out), .sel(and_9_out));
  Decoder #(.select(2), .disabled(0), .enable("false")) decoder_1 (
    .out0(decoder_1_out0), .out1(decoder_1_out1), .out2(decoder_1_out2), .out3(decoder_1_out3), .sel(Step_q));
  and and_2 (and_2_out, multiplexer_2_out[0], multiplexer_2_out[1]);
  and and_3 (and_3_out, and_2_out, and_4_out);
  and and_4 (and_4_out, multiplexer_2_out[2], multiplexer_2_out[3]);
  and and_5 (and_5_out, multiplexer_2_out[4], multiplexer_2_out[5]);
  and and_6 (and_6_out, and_5_out, and_7_out);
  and and_7 (and_7_out, multiplexer_2_out[6], multiplexer_2_out[7]);
  RAM #(.bus("separate")) ram_1 (
    .addr(multiplexer_2_out), .din(multiplexer_7_out), .data(ram_1_data), .str(decoder_2_out2),
    .clk(and_1_out));  // open: sel, ld, clr
  and and_8 (and_8_out, and_3_out, and_6_out);
  TTY tty_1 (.data(multiplexer_7_out[6:0]), .clk(and_1_out), .we(and_8_out), .clr(Reset_out));
  Register Instruction_byte (
    .D(ram_1_data), .en(decoder_1_out0), .Q(Instruction_byte_q), .clk(and_1_out), .clr(Reset_out));
  and and_9 (and_9_out, decoder_1_out2, Instruction_byte_q[1]);
  Register Data_byte (.D(ram_1_data), .en(decoder_1_out1), .Q(Data_byte_q), .clk(and_1_out), .clr(Reset_out));
  Multiplexer #(.width(8), .enable("false")) multiplexer_3 (
    .in0(Data_byte_q), .in1(multiplexer_8_out), .out(multiplexer_3_out), .sel(Instruction_byte_q[0]));
  Decoder #(.select(5), .disabled(0)) decoder_2 (
    .out1(decoder_2_out1), .out2(decoder_2_out2), .out3(decoder_2_out3), .out4(decoder_2_out4),
    .out5(decoder_2_out5), .out6(decoder_2_out6), .out7(decoder_2_out7), .out8(decoder_2_out8),
    .out9(decoder_2_out9), .out10(decoder_2_out10), .out11(decoder_2_out11), .out12(decoder_2_out12),
    .out13(decoder_2_out13), .out14(decoder_2_out14), .out15(decoder_2_out15), .out16(decoder_2_out16),
    .out17(decoder_2_out17), .out18(decoder_2_out18), .out19(decoder_2_out19), .out20(decoder_2_out20),
    .out31(decoder_2_out31), .sel(Instruction_byte_q[7:3]), .en(decoder_1_out2));  // open: out0, out21, out22, out23, out24, out25, out26, out27, out28, out29, out30
  Multiplexer #(.select(2), .width(8), .enable("false")) multiplexer_4 (
    .in0(Data_byte_q), .in1(multiplexer_8_out), .in2(ram_1_data), .in3(ram_1_data),
    .out({multiplexer_4_out_2, multiplexer_4_out}), .sel(Instruction_byte_q[1:0]));
  or ADD (ADD_out, decoder_2_out3, decoder_2_out4);
  or Bit (Bit_out, decoder_2_out8, decoder_2_out9);
  or S_C (S_C_out, decoder_2_out5, decoder_2_out7);
  or Bit_2 (Bit_2_out, Bit_out, decoder_2_out10);
  or Bit_3 (Bit_3_out, Bit_2_out, decoder_2_out11);
  or Bit_4 (Bit_4_out, Bit_3_out, decoder_2_out12);
  or SUB (SUB_out, decoder_2_out6, S_C_out);
  or CF (CF_out, ADD_out, SUB_out);
  or ZF (ZF_out, CF_out, Bit_5_out);
  or ENABLE (ENABLE_out, ZF_out, decoder_2_out1);
  or Bit_5 (Bit_5_out, Bit_4_out, decoder_2_out13);
  not not_2 (not_2_out, decoder_2_out7);
  and NO_CMP (NO_CMP_out, not_2_out, ENABLE_out);
  not not_3 (not_3_out, Carry_flag_q);
  not not_4 (not_4_out, Zero_flag_q);
  _3_bit_dedecoder u_3_bit_dedecoder_1 (
    .in_1(CF_out), .in_2(decoder_2_out8), .in_3(decoder_2_out9), .in_4(decoder_2_out10),
    .in_5(decoder_2_out11), .in_6(decoder_2_out12), .in_7(decoder_2_out13), .out_8(n3_bit_dedecoder_1_out_8));
  Multiplexer #(.width(8), .enable("false")) multiplexer_5 (
    .in0({multiplexer_4_out_2, multiplexer_4_out}), .in1(not_5_out), .out(multiplexer_5_out), .sel(SUB_out));
  assign not_5_out = ~{multiplexer_4_out_2, multiplexer_4_out};  // NOT_Gate not_5, 8 bits wide
  nor nor_1 (nor_1_out, multiplexer_6_out[0], multiplexer_6_out[1]);
  and and_10 (and_10_out, nor_1_out, nor_2_out);
  nor nor_2 (nor_2_out, multiplexer_6_out[2], multiplexer_6_out[3]);
  nor nor_3 (nor_3_out, multiplexer_6_out[4], multiplexer_6_out[5]);
  and and_11 (and_11_out, nor_3_out, nor_4_out);
  nor nor_4 (nor_4_out, multiplexer_6_out[6], multiplexer_6_out[7]);
  and JC (JC_out, decoder_2_out15, Carry_flag_q);
  and JNC (JNC_out, decoder_2_out16, not_3_out);
  and JZ (JZ_out, decoder_2_out17, Zero_flag_q);
  and JNZ (JNZ_out, decoder_2_out18, not_4_out);
  and ADC (ADC_out, Carry_flag_q, decoder_2_out4);
  not not_6 (not_6_out, Carry_flag_q);
  or C (C_out, ADC_out, SBB_out);
  and SBB (SBB_out, not_6_out, decoder_2_out6);
  or C_2 (C_2_out, S_C_out, C_out);
  Adder adder_3 (.a(multiplexer_7_out), .b(multiplexer_5_out), .out(adder_3_out), .cin(C_2_out), .cout(adder_3_cout));
  assign and_12_out = multiplexer_7_out & {multiplexer_4_out_2, multiplexer_4_out};  // AND_Gate and_12, 8 bits wide
  assign or_3_out = multiplexer_7_out | {multiplexer_4_out_2, multiplexer_4_out};  // OR_Gate or_3, 8 bits wide
  assign xor_1_out = multiplexer_7_out ^ {multiplexer_4_out_2, multiplexer_4_out};  // XOR_Gate xor_1, 8 bits wide
  assign not_7_out = ~{multiplexer_4_out_2, multiplexer_4_out};  // NOT_Gate not_7, 8 bits wide
  Shifter shifter_1 (.in(multiplexer_7_out), .\dist (multiplexer_4_out), .out(shifter_1_out));
  Shifter #(.shift("lr")) shifter_2 (.in(multiplexer_7_out), .\dist (multiplexer_4_out), .out(shifter_2_out));
  and and_13 (and_13_out, and_10_out, and_11_out);
  or JMP (JMP_out, decoder_2_out14, JC_out);
  or JMP_2 (JMP_2_out, JMP_out, JNC_out);
  nor JA (JA_out, Carry_flag_q, Zero_flag_q);
  and JNA (JNA_out, Carry_flag_q, Zero_flag_q);
  D_Flip_Flop Carry_flag (
    .clk(and_1_out), .D(adder_3_cout), .Q(Carry_flag_q), .en(CF_out), .reset(Reset_out));  // open: Qn, preset
  D_Flip_Flop Zero_flag (
    .clk(and_1_out), .D(and_13_out), .Q(Zero_flag_q), .en(ZF_out), .reset(Reset_out));  // open: Qn, preset
  or JMP_3 (JMP_3_out, JMP_2_out, JZ_out);
  or JMP_4 (JMP_4_out, JMP_3_out, JNZ_out);
  and JA_2 (JA_2_out, JA_out, decoder_2_out19);
  and JNA_2 (JNA_2_out, JNA_out, decoder_2_out20);
  Decoder #(.disabled(0)) decoder_3 (
    .out0(decoder_3_out0), .out1(decoder_3_out1), .sel(Instruction_byte_q[2]), .en(NO_CMP_out));
  Multiplexer #(.select(3), .width(8), .enable("false")) multiplexer_6 (
    .in0({multiplexer_4_out_2, multiplexer_4_out}), .in1(adder_3_out), .in2(and_12_out), .in3(or_3_out),
    .in4(xor_1_out), .in5(not_7_out), .in6(shifter_1_out), .in7(shifter_2_out), .out(multiplexer_6_out),
    .sel(n3_bit_dedecoder_1_out_8));
  or JMP_5 (JMP_5_out, JMP_4_out, JA_2_out);
  or JMP_6 (JMP_6_out, JMP_5_out, JNA_2_out);
  Register A (.D(multiplexer_6_out), .en(decoder_3_out0), .Q(A_q), .clk(and_1_out), .clr(Reset_out));
  Multiplexer #(.width(8), .enable("false")) multiplexer_7 (
    .in0(A_q), .in1(B_q), .out(multiplexer_7_out), .sel(Instruction_byte_q[2]));
  Multiplexer #(.width(8), .enable("false")) multiplexer_8 (
    .in0(A_q), .in1(B_q), .out(multiplexer_8_out), .sel(Data_byte_q[0]));
  Register B (.D(multiplexer_6_out), .en(decoder_3_out1), .Q(B_q), .clk(and_1_out), .clr(Reset_out));

  // Notes on the sheet:
  //   The Neva 8-bit Processor
  //   Made by Bastiaan van der Plaat
endmodule

module _3_bit_dedecoder (
  input  in_1,
  input  in_2,
  input  in_3,
  input  in_4,
  input  in_5,
  input  in_6,
  input  in_7,
  output [2:0] out_8
);

  wire or_1_out, or_2_out, or_3_out, or_4_out, or_5_out, or_6_out;

  or or_1 (or_1_out, in_3, in_1);
  or or_2 (or_2_out, in_3, in_2);
  or or_3 (or_3_out, in_5, in_4);
  or or_4 (or_4_out, or_1_out, in_5);
  or or_5 (or_5_out, or_2_out, in_6);
  or or_6 (or_6_out, or_3_out, in_6);
  or or_7 (out_8[0], in_7, or_4_out);
  or or_8 (out_8[1], in_7, or_5_out);
  or or_9 (out_8[2], in_7, or_6_out);
endmodule
